// Logisim project 8bit ALU.circ as structural Verilog: 2 circuits, main circuit 1b ALU
module _1b_ALU (
  input  Sub,
  input  Cin,
  input  [2:0] in_3,
  input  A,
  input  B,
  input  Less,
  output out_7,
  output Cout,
  output Set
);

  wire and_1_out, nor_1_out, or_1_out, xor_1_out, xor_2_out;

  xor xor_1 (xor_1_out, B, Sub);
  and and_1 (and_1_out, A, B);
  or or_1 (or_1_out, A, B);
  xor xor_2 (xor_2_out, A, B);
  nor nor_1 (nor_1_out, A, B);
  Adder #(.width(1)) adder_1 (.a(A), .b(xor_1_out), .out(Set), .cin(Cin), .cout(Cout));
  Multiplexer #(.select(3), .enable("false")) multiplexer_1 (
    .in0(and_1_out), .in1(or_1_out), .in2(xor_2_out), .in3(nor_1_out), .in4(Set), .in5(Less), .out(out_7),
    .sel(in_3));  // open: in6, in7
endmodule

module _8b_alu (
  input  Sub,
  input  [2:0] Select,
  input  [7:0] A,
  input  [7:0] A_2,
  output [7:0] Result,
  output Zero
);

  wire n1b_alu_1_cout, n1b_alu_2_cout, n1b_alu_3_cout, n1b_alu_4_cout, n1b_alu_5_cout, n1b_alu_6_cout,
       n1b_alu_7_cout, n1b_alu_8_set;

  _1b_ALU u_1b_alu_1 (
    .A(A[0]), .B(A_2[0]), .Less(n1b_alu_8_set), .Sub(Sub), .Cin(Sub), .in_3(Select), .out_7(Result[0]),
    .Cout(n1b_alu_1_cout));  // open: Set
  _1b_ALU u_1b_alu_2 (
    .A(A[1]), .B(A_2[1]), .Less(1'b0), .Sub(Sub), .Cin(n1b_alu_1_cout), .in_3(Select), .out_7(Result[1]),
    .Cout(n1b_alu_2_cout));  // open: Set
  _1b_ALU u_1b_alu_3 (
    .A(A[2]), .B(A_2[2]), .Less(1'b0), .Sub(Sub), .Cin(n1b_alu_2_cout), .in_3(Select), .out_7(Result[2]),
    .Cout(n1b_alu_3_cout));  // open: Set
  _1b_ALU u_1b_alu_4 (
    .A(A[3]), .B(A_2[3]), .Less(1'b0), .Sub(Sub), .Cin(n1b_alu_3_cout), .in_3(Select), .out_7(Result[3]),
    .Cout(n1b_alu_4_cout));  // open: Set
  _1b_ALU u_1b_alu_5 (
    .A(A[4]), .B(A_2[4]), .Less(1'b0), .Sub(Sub), .Cin(n1b_alu_4_cout), .in_3(Select), .out_7(Result[4]),
    .Cout(n1b_alu_5_cout));  // open: Set
  _1b_ALU u_1b_alu_6 (
    .A(A[5]), .B(A_2[5]), .Less(1'b0), .Sub(Sub), .Cin(n1b_alu_5_cout), .in_3(Select), .out_7(Result[5]),
    .Cout(n1b_alu_6_cout));  // open: Set
  _1b_ALU u_1b_alu_7 (
    .A(A[6]), .B(A_2[6]), .Less(1'b0), .Sub(Sub), .Cin(n1b_alu_6_cout), .in_3(Select), .out_7(Result[6]),
    .Cout(n1b_alu_7_cout));  // open: Set
  _1b_ALU u_1b_alu_8 (
    .A(A[7]), .B(A_2[7]), .Less(1'b0), .Sub(Sub), .Cin(n1b_alu_7_cout), .in_3(Select), .out_7(Result[7]),
    .Set(n1b_alu_8_set));  // open: Cout
  nor nor_1 (Zero, Result[0], Result[1], Result[2], Result[3], Result[4], Result[5], Result[6], Result[7]);
endmodule
